// Logisim project PA2_Hamming_Code_Circuit.circ as structural Verilog: 1 circuit, main circuit main
module main (
  input  in_1,
  input  [2:0] in_2,
  input  [2:0] in_3,
  input  [2:0] in_4,
  input  [2:0] in_5,
  input  [2:0] in_6,
  input  in_7,
  input  in_8,
  input  [2:0] in_9,
  input  in_10,
  input  [2:0] in_11,
  input  [2:0] in_12,
  output a3,
  output r2,
  output a2,
  output r1,
  output a1,
  output r0,
  output a0,
  output q2,
  output [2:0] out_21,
  output q1,
  output q0,
  output b3,
  output b2,
  output b1,
  output b0
);

  wire a1_a0_out, a3_a2_out, and_1_out, and_2_out, and_3_out, b0_2_out, b0_out, b1_2_out, b1_out, b2_2_out,
       b2_out, b3_2_out, Button_1_out, Button_2_out, Button_3_out, Button_4_out, Button_5_out, Button_6_out,
       Button_7_out, Button_8_out, Button_9_out, Button_10_out, Button_11_out, Button_12_out, Button_13_out,
       Button_14_out, Button_15_out, Button_16_out, nor_1_out, nor_2_out, nor_3_out, not_2_out, not_3_out,
       not_4_out, q0_out, q1_out, q2_out;
  wire [2:0] s2_out;
  wire [3:0] a0_out;

  Button Button_1 (.out(Button_1_out));
  Button Button_2 (.out(Button_2_out));
  Button Button_3 (.out(Button_3_out));
  Button Button_4 (.out(Button_4_out));
  Button Button_5 (.out(Button_5_out));
  Button Button_6 (.out(Button_6_out));
  Button Button_7 (.out(Button_7_out));
  Button Button_8 (.out(Button_8_out));
  Button Button_9 (.out(Button_9_out));
  Button Button_10 (.out(Button_10_out));
  Button Button_11 (.out(Button_11_out));
  Button Button_12 (.out(Button_12_out));
  Button Button_13 (.out(Button_13_out));
  Button Button_14 (.out(Button_14_out));
  Button Button_15 (.out(Button_15_out));
  Button Button_16 (.out(Button_16_out));
  Priority_Encoder #(.select(4)) priority_encoder_1 (
    .in0(Button_1_out), .in1(Button_2_out), .in2(Button_3_out), .in3(Button_4_out), .in4(Button_5_out),
    .in5(Button_6_out), .in6(Button_7_out), .in7(Button_8_out), .in8(Button_9_out), .in9(Button_10_out),
    .in10(Button_11_out), .in11(Button_12_out), .in12(Button_13_out), .in13(Button_14_out),
    .in14(Button_15_out), .in15(Button_16_out), .out({a3, a2, a1, a0}));  // open: gs, en_out, en_in
  Hex_Digit_Display hex_digit_display_1 (.value({a3, a2, a1, a0}));  // open: dp
  not not_1 (b0, a0);
  not not_2 (not_2_out, b0);
  xor a3_a2 (a3_a2_out, a3, a2);
  xor a1_a0 (a1_a0_out, a1, a0);
  // XOR_Gate b3 has open pins: in1=a3, in3=a3, out=open
  xor u_b2 (b2_out, a2, a2);
  xor u_b1 (b1_out, a1, a1);
  xor u_b0 (b0_out, a0, not_2_out);
  Hex_Digit_Display hex_digit_display_2 (.value({a3, a2, a1, b0}));  // open: dp
  xor u_r2 (q2, a3_a2_out, a1);
  xor u_r1 (r1, a3_a2_out, a0);
  xor u_r0 (r0, a3, a1_a0_out);
  not not_3 (not_3_out, q1);
  not not_4 (not_4_out, q0);
  not not_5 (q1, r1);
  not not_6 (q0, r0);
  Hex_Digit_Display hex_digit_display_3 (.value({q2, r1, r0, in_1}));  // open: dp
  xor u_q2 (q2_out, q2, q2);
  xor u_q1 (q1_out, r1, not_3_out);
  xor u_q0 (q0_out, r0, not_4_out);
  nor nor_1 (nor_1_out, q2_out, q1_out);
  nor nor_2 (nor_2_out, q1_out, q0_out);
  nor nor_3 (nor_3_out, q2_out, q0_out);
  Hex_Digit_Display hex_digit_display_4 (.value({q2, q1, q0, in_8}));  // open: dp
  nor s2 (s2_out[0], nor_1_out, b2_out);
  nor s1 (s2_out[1], nor_3_out, b1_out);
  nor s0 (s2_out[2], nor_2_out, b0_out);
  and and_1 (and_1_out, out_21[0], out_21[1]);
  and and_2 (and_2_out, out_21[1], out_21[2]);
  and and_3 (and_3_out, out_21[0], out_21[2]);
  Multiplexer #(.select(3), .width(3)) multiplexer_1 (
    .in0(in_2), .in1(in_3), .in2(in_4), .in3(in_5), .in4(in_6), .in5(in_9), .in6(in_11), .in7(in_12),
    .out(out_21), .sel(s2_out), .en(in_10));
  xor b0_2 (b0_2_out, and_1_out, out_21[2]);
  xor b1_2 (b1_2_out, out_21[1], and_3_out);
  xor b2_2 (b2_2_out, out_21[0], and_2_out);
  and b3_2 (b3_2_out, out_21[0], and_2_out);
  Hex_Digit_Display hex_digit_display_5 (.value({in_7, out_21}));  // open: dp
  Hex_Digit_Display hex_digit_display_6 (.value(a0_out));  // open: dp
  xor u_a0 (a0_out[0], b0_2_out, a0);
  xor u_a1 (a0_out[1], b1_2_out, a1);
  xor u_a2 (a0_out[2], b2_2_out, a2);
  xor u_a3 (a0_out[3], b3_2_out, a3);

  assign b1 = a1;
  assign b2 = a2;
  assign b3 = a3;
  assign r2 = q2;

  // Notes on the sheet:
  //   a3a2a1a0
  //   b3b2b1b0
  //   r2r1r0
  //   q2q1q0
  //   s2s1s0
  //   a3a2a1a0
endmodule
